# Fritzing sketch Ford Puma Future  Engineers (saved by Fritzing 0.9.3b)

parts:
  Part1 = SRF05 Ultrasonic Rangefinder
  Part2 = SRF05 Ultrasonic Rangefinder
  S1 = H-Bridge with L298N
  Mod2 = Microbit
  A1 = HuskyLens-Vision-Sensor_1  # not connected
  Bat1 = battery_holder_single_18650
  Bat2 = battery_holder_single_18650
  M1 = DC Motor
  M2 = DC Motor
  Part3 = SRF05 Ultrasonic Rangefinder

nets:
  N1: Part1.Trig, Mod2.P14
  N2: Part1.Echo, Mod2.P13
  N3: Part2.Trig, Mod2.P16
  N4: Part2.Echo, Mod2.P15
  N5: S1.12V, Bat1.+#1
  N6: S1.GND, Bat2.+#0
  N7: S1.ENA, S1.ENA-5V
  N8: S1.IN1, Mod2.P11
  N9: S1.IN2, Mod2.P10
  N10: S1.IN3, Mod2.P9
  N11: S1.IN4, Mod2.P8
  N12: S1.ENB, Mod2.P1
  N13: S1.M1-01, M2.pin_2
  N14: S1.M1-02, S1.M2-02, M1.pin_1, M2.pin_1
  N15: S1.M2-01, M1.pin_2
  N16: Mod2.P12, Part3.Echo
  N17: Mod2.P2, Part3.Trig
  N18: Bat1.+#0, Bat2.+#1

custom parts:
  H-Bridge with L298N: h-bridge
  Microbit: BBC Microbit Fritzing part. May 2019 expanded to include schematic and pcb views as well as breadboard. PCB view assumes an Adafruit PRODUCT ID: 3342 2x40 Right Angle through hole edge connector (although others will probably work as well). The pcb svg is custom (see forum article http://forum.fritzing.org/t/making-edge-connectors-and-both-side-smd-parts/7287 for an explaination if you need to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
  HuskyLens-Vision-Sensor_1: Huskylens is an easy-to-use AI Camera | Vision Sensor. DFrobot Huskylens is equipped with multiple functions, such as face recognition, object tracking, object recognition, line tracking, color recognition, and tag(QR code) recognition.
  battery_holder_single_18650: single 18650 battery holder
